// Logisim project ALU_4BIT.circ as structural Verilog: 17 circuits, main circuit AND_Gate_4bit
module AND_Gate_4bit (
  input  [3:0] A,
  input  [3:0] B,
  output [3:0] O
);

  and and_1 (O[3], B[3], A[3]);
  and and_2 (O[2], B[2], A[2]);
  and and_3 (O[1], B[1], A[1]);
  and and_4 (O[0], A[0], B[0]);

  // Notes on the sheet:
  //   4bit AND gate
endmodule

module OR_Gate_4bit (
  input  [3:0] A,
  input  [3:0] B,
  output [3:0] O
);

  or or_1 (O[3], B[3], A[3]);
  or or_2 (O[2], B[2], A[2]);
  or or_3 (O[1], B[1], A[1]);
  or or_4 (O[0], A[0], B[0]);

  // Notes on the sheet:
  //   4 bit OR Gate
endmodule

module XOR_Gate (
  input  [3:0] A,
  input  [3:0] B,
  output [3:0] O
);

  xor xor_1 (O[3], B[3], A[3]);
  xor xor_2 (O[2], B[2], A[2]);
  xor xor_3 (O[1], B[1], A[1]);
  xor xor_4 (O[0], A[0], B[0]);

  // Notes on the sheet:
  //   4 bit XOR Gate
endmodule

module NOT_Gate_4bit (
  input  [3:0] A,
  output [3:0] O
);

  not not_1 (O[3], A[3]);
  not not_2 (O[2], A[2]);
  not not_3 (O[1], A[1]);
  not not_4 (O[0], A[0]);

  // Notes on the sheet:
  //   4 bit NOT Gate
endmodule

module FS (
  input  A,
  input  B,
  input  Bin,
  output D,
  output Bout
);

  wire and_1_out, and_2_out, not_1_out, not_2_out, xor_1_out;

  not not_1 (not_1_out, A);
  xor xor_1 (xor_1_out, A, B);
  not not_2 (not_2_out, xor_1_out);
  and and_1 (and_1_out, B, not_1_out);
  xor xor_2 (D, xor_1_out, Bin);
  and and_2 (and_2_out, Bin, not_2_out);
  or or_1 (Bout, and_2_out, and_1_out);

  // Notes on the sheet:
  //   1 bit Full Subtractor Circuit
endmodule

module Adder_Subtractor_4bit (
  input  [3:0] A,
  input  Sel,
  input  [3:0] B,
  output Carry,
  output [3:0] O
);

  wire fa_2_cout, fa_3_cout, fa_4_cout, xor_1_out, xor_2_out, xor_3_out, xor_4_out;

  xor xor_1 (xor_1_out, B[3], Sel);
  FA fa_1 (.a(A[3]), .b(xor_1_out), .Cin(fa_2_cout), .S(O[3]), .Cout(Carry));
  xor xor_2 (xor_2_out, B[2], Sel);
  FA fa_2 (.a(A[2]), .b(xor_2_out), .Cin(fa_3_cout), .S(O[2]), .Cout(fa_2_cout));
  xor xor_3 (xor_3_out, B[1], Sel);
  FA fa_3 (.a(A[1]), .b(xor_3_out), .Cin(fa_4_cout), .S(O[1]), .Cout(fa_3_cout));
  xor xor_4 (xor_4_out, B[0], Sel);
  FA fa_4 (.a(A[0]), .b(xor_4_out), .Cin(Sel), .S(O[0]), .Cout(fa_4_cout));

  // Notes on the sheet:
  //   4 bit Adder and Subtractor Circuit
endmodule

module FA (
  input  a,
  input  b,
  input  Cin,
  output S,
  output Cout
);

  wire and_1_out, and_2_out, xor_1_out;

  xor xor_1 (xor_1_out, a, b);
  and and_1 (and_1_out, b, a);
  xor xor_2 (S, xor_1_out, Cin);
  and and_2 (and_2_out, Cin, xor_1_out);
  or or_1 (Cout, and_2_out, and_1_out);

  // Notes on the sheet:
  //   1 bit Adder Circuit
endmodule

module Left_Shifter_4bit (
  input  [3:0] A,
  input  [1:0] Shift,
  output [3:0] O
);

  Multiplexer #(.select(2)) multiplexer_1 (.in0(A[3]), .in1(A[2]), .in2(A[1]), .in3(A[0]), .out(O[3]), .sel(Shift));
  Multiplexer #(.select(2)) multiplexer_2 (.in0(A[2]), .in1(A[1]), .in2(A[0]), .in3(1'b0), .out(O[2]), .sel(Shift));
  Multiplexer #(.select(2)) multiplexer_3 (.in0(A[1]), .in1(A[0]), .in2(1'b0), .in3(1'b0), .out(O[1]), .sel(Shift));
  Multiplexer #(.select(2)) multiplexer_4 (.in0(A[0]), .in1(1'b0), .in2(1'b0), .in3(1'b0), .out(O[0]), .sel(Shift));

  // Notes on the sheet:
  //   4 bit Left Shifter
endmodule

module Right_Shifter_4bit (
  input  [3:0] A,
  input  [1:0] Shift,
  output [3:0] O
);

  Multiplexer #(.select(2)) multiplexer_1 (.in0(A[3]), .in1(1'b0), .in2(1'b0), .in3(1'b0), .out(O[3]), .sel(Shift));
  Multiplexer #(.select(2)) multiplexer_2 (.in0(A[2]), .in1(A[3]), .in2(1'b0), .in3(1'b0), .out(O[2]), .sel(Shift));
  Multiplexer #(.select(2)) multiplexer_3 (.in0(A[1]), .in1(A[2]), .in2(A[3]), .in3(1'b0), .out(O[1]), .sel(Shift));
  Multiplexer #(.select(2)) multiplexer_4 (.in0(A[0]), .in1(A[1]), .in2(A[2]), .in3(A[3]), .out(O[0]), .sel(Shift));

  // Notes on the sheet:
  //   4 bit Right Shifter
endmodule

module Left_Rotate_4bit (
  input  [3:0] A,
  input  [1:0] Shift,
  output [3:0] O
);

  Multiplexer #(.select(2)) multiplexer_1 (.in0(A[3]), .in1(A[2]), .in2(A[1]), .in3(A[0]), .out(O[3]), .sel(Shift));
  Multiplexer #(.select(2)) multiplexer_2 (.in0(A[2]), .in1(A[1]), .in2(A[0]), .in3(A[3]), .out(O[2]), .sel(Shift));
  Multiplexer #(.select(2)) multiplexer_3 (.in0(A[1]), .in1(A[0]), .in2(A[3]), .in3(A[2]), .out(O[1]), .sel(Shift));
  Multiplexer #(.select(2)) multiplexer_4 (.in0(A[0]), .in1(A[3]), .in2(A[2]), .in3(A[1]), .out(O[0]), .sel(Shift));

  // Notes on the sheet:
  //   4 bit Left Rotator
endmodule

module Right_Rotate_4bit (
  input  [3:0] A,
  input  [1:0] Shift,
  output [3:0] O
);

  Multiplexer #(.select(2)) multiplexer_1 (.in0(A[3]), .in1(A[0]), .in2(A[1]), .in3(A[2]), .out(O[3]), .sel(Shift));
  Multiplexer #(.select(2)) multiplexer_2 (.in0(A[2]), .in1(A[3]), .in2(A[0]), .in3(A[1]), .out(O[2]), .sel(Shift));
  Multiplexer #(.select(2)) multiplexer_3 (.in0(A[1]), .in1(A[2]), .in2(A[3]), .in3(A[0]), .out(O[1]), .sel(Shift));
  Multiplexer #(.select(2)) multiplexer_4 (.in0(A[0]), .in1(A[1]), .in2(A[2]), .in3(A[3]), .out(O[0]), .sel(Shift));

  // Notes on the sheet:
  //   4 bit Right Rotator
endmodule

module Cell_M (
  input  x,
  input  y,
  input  b,
  input  Cin,
  output Cout,
  output x_copy,
  output s
);

  wire and_1_out;

  and and_1 (and_1_out, x, y);
  FA fa_1 (.a(b), .b(and_1_out), .Cin(Cin), .S(s), .Cout(Cout));

  assign x_copy = x;
endmodule

module Unsigned_Multiplier_4bit (
  input  [3:0] B,
  input  [3:0] A,
  output OverFlow,
  output [3:0] O
);

  wire cell_m_1_cout, cell_m_1_s, cell_m_2_cout, cell_m_2_s, cell_m_2_x_copy, cell_m_3_cout, cell_m_3_s,
       cell_m_4_cout, cell_m_4_s, cell_m_4_x_copy, cell_m_5_cout, cell_m_5_s, cell_m_5_x_copy, cell_m_6_cout,
       cell_m_6_s, cell_m_7_cout, cell_m_7_s, cell_m_7_x_copy, cell_m_8_cout, cell_m_8_s, cell_m_8_x_copy,
       cell_m_9_cout, cell_m_9_s, cell_m_9_x_copy, cell_m_10_cout, cell_m_11_cout, cell_m_11_s,
       cell_m_11_x_copy, cell_m_12_cout, cell_m_12_s, cell_m_12_x_copy, cell_m_13_cout, cell_m_13_x_copy,
       cell_m_14_cout, cell_m_14_s, cell_m_14_x_copy, cell_m_15_cout, cell_m_15_x_copy, cell_m_16_cout,
       cell_m_16_x_copy;

  Cell_M cell_m_1 (
    .x(cell_m_2_x_copy), .y(B[3]), .b(cell_m_2_cout), .Cin(cell_m_3_cout), .Cout(cell_m_1_cout),
    .s(cell_m_1_s));  // open: x_copy
  Cell_M cell_m_2 (
    .x(cell_m_4_x_copy), .y(B[2]), .b(cell_m_4_cout), .Cin(cell_m_5_cout), .Cout(cell_m_2_cout),
    .x_copy(cell_m_2_x_copy), .s(cell_m_2_s));
  Cell_M cell_m_3 (
    .x(cell_m_5_x_copy), .y(B[3]), .b(cell_m_2_s), .Cin(cell_m_6_cout), .Cout(cell_m_3_cout), .s(cell_m_3_s));  // open: x_copy
  Cell_M cell_m_4 (
    .x(cell_m_7_x_copy), .y(B[1]), .b(cell_m_7_cout), .Cin(cell_m_8_cout), .Cout(cell_m_4_cout),
    .x_copy(cell_m_4_x_copy), .s(cell_m_4_s));
  Cell_M cell_m_5 (
    .x(cell_m_8_x_copy), .y(B[2]), .b(cell_m_4_s), .Cin(cell_m_9_cout), .Cout(cell_m_5_cout),
    .x_copy(cell_m_5_x_copy), .s(cell_m_5_s));
  Cell_M cell_m_6 (
    .x(cell_m_9_x_copy), .y(B[3]), .b(cell_m_5_s), .Cin(cell_m_10_cout), .Cout(cell_m_6_cout), .s(cell_m_6_s));  // open: x_copy
  Cell_M cell_m_7 (
    .x(A[3]), .y(B[0]), .b(1'b0), .Cin(cell_m_11_cout), .Cout(cell_m_7_cout), .x_copy(cell_m_7_x_copy),
    .s(cell_m_7_s));
  Cell_M cell_m_8 (
    .x(cell_m_11_x_copy), .y(B[1]), .b(cell_m_7_s), .Cin(cell_m_12_cout), .Cout(cell_m_8_cout),
    .x_copy(cell_m_8_x_copy), .s(cell_m_8_s));
  Cell_M cell_m_9 (
    .x(cell_m_12_x_copy), .y(B[2]), .b(cell_m_8_s), .Cin(cell_m_13_cout), .Cout(cell_m_9_cout),
    .x_copy(cell_m_9_x_copy), .s(cell_m_9_s));
  Cell_M cell_m_10 (
    .x(cell_m_13_x_copy), .y(B[3]), .b(cell_m_9_s), .Cin(1'b0), .Cout(cell_m_10_cout), .s(O[3]));  // open: x_copy
  Cell_M cell_m_11 (
    .x(A[2]), .y(B[0]), .b(1'b0), .Cin(cell_m_14_cout), .Cout(cell_m_11_cout), .x_copy(cell_m_11_x_copy),
    .s(cell_m_11_s));
  Cell_M cell_m_12 (
    .x(cell_m_14_x_copy), .y(B[1]), .b(cell_m_11_s), .Cin(cell_m_15_cout), .Cout(cell_m_12_cout),
    .x_copy(cell_m_12_x_copy), .s(cell_m_12_s));
  Cell_M cell_m_13 (
    .x(cell_m_15_x_copy), .y(B[2]), .b(cell_m_12_s), .Cin(1'b0), .Cout(cell_m_13_cout),
    .x_copy(cell_m_13_x_copy), .s(O[2]));
  or or_1 (OverFlow, cell_m_6_s, cell_m_3_s, cell_m_1_s, cell_m_1_cout);
  Cell_M cell_m_14 (
    .x(A[1]), .y(B[0]), .b(1'b0), .Cin(cell_m_16_cout), .Cout(cell_m_14_cout), .x_copy(cell_m_14_x_copy),
    .s(cell_m_14_s));
  Cell_M cell_m_15 (
    .x(cell_m_16_x_copy), .y(B[1]), .b(cell_m_14_s), .Cin(1'b0), .Cout(cell_m_15_cout),
    .x_copy(cell_m_15_x_copy), .s(O[1]));
  Cell_M cell_m_16 (
    .x(A[0]), .y(B[0]), .b(1'b0), .Cin(1'b0), .Cout(cell_m_16_cout), .x_copy(cell_m_16_x_copy), .s(O[0]));

  // Notes on the sheet:
  //   4 bit Unsigned Multiplier Circuit
endmodule

module Cell_D (
  input  A,
  input  B,
  input  Bin,
  input  Sel,
  output Bout,
  output A_D,
  output Sel_copy,
  output B_copy
);

  wire fs_1_d;

  FS fs_1 (.A(A), .B(B), .Bin(Bin), .D(fs_1_d), .Bout(Bout));
  Multiplexer multiplexer_1 (.in0(fs_1_d), .in1(A), .out(A_D), .sel(Sel));

  assign B_copy = B;
  assign Sel_copy = Sel;
endmodule

module Unsigned_divider_4bit (
  input  [3:0] A,
  input  [3:0] B,
  output Exception,
  output [3:0] O
);

  wire cell_d_1_b_copy, cell_d_1_bout, cell_d_1_sel_copy, cell_d_2_a_d, cell_d_2_b_copy, cell_d_2_bout,
       cell_d_2_sel_copy, cell_d_3_b_copy, cell_d_3_bout, cell_d_3_sel_copy, cell_d_4_a_d, cell_d_4_b_copy,
       cell_d_4_bout, cell_d_4_sel_copy, cell_d_5_a_d, cell_d_5_b_copy, cell_d_5_bout, cell_d_5_sel_copy,
       cell_d_6_b_copy, cell_d_6_bout, cell_d_6_sel_copy, cell_d_7_a_d, cell_d_7_b_copy, cell_d_7_bout,
       cell_d_8_a_d, cell_d_8_b_copy, cell_d_8_bout, cell_d_8_sel_copy, cell_d_9_a_d, cell_d_9_b_copy,
       cell_d_9_bout, cell_d_9_sel_copy, cell_d_10_bout, cell_d_10_sel_copy, cell_d_11_a_d, cell_d_11_b_copy,
       cell_d_11_bout, cell_d_12_a_d, cell_d_12_b_copy, cell_d_12_bout, cell_d_12_sel_copy, cell_d_13_bout,
       cell_d_13_sel_copy, cell_d_14_a_d, cell_d_14_b_copy, cell_d_14_bout, cell_d_15_bout,
       cell_d_15_sel_copy, cell_d_16_bout;

  not not_1 (O[3], cell_d_1_bout);
  Cell_D cell_d_1 (
    .Sel(cell_d_1_bout), .A(1'b0), .B(B[3]), .Bin(cell_d_2_bout), .Bout(cell_d_1_bout),
    .Sel_copy(cell_d_1_sel_copy), .B_copy(cell_d_1_b_copy));  // open: A_D
  not not_2 (O[2], cell_d_3_bout);
  not not_3 (O[1], cell_d_6_bout);
  Cell_D cell_d_2 (
    .Sel(cell_d_1_sel_copy), .A(1'b0), .B(B[2]), .Bin(cell_d_4_bout), .Bout(cell_d_2_bout),
    .A_D(cell_d_2_a_d), .Sel_copy(cell_d_2_sel_copy), .B_copy(cell_d_2_b_copy));
  Cell_D cell_d_3 (
    .Sel(cell_d_3_bout), .A(cell_d_2_a_d), .B(cell_d_1_b_copy), .Bin(cell_d_5_bout), .Bout(cell_d_3_bout),
    .Sel_copy(cell_d_3_sel_copy), .B_copy(cell_d_3_b_copy));  // open: A_D
  not not_4 (O[0], cell_d_10_bout);
  Cell_D cell_d_4 (
    .Sel(cell_d_2_sel_copy), .A(1'b0), .B(B[1]), .Bin(cell_d_7_bout), .Bout(cell_d_4_bout),
    .A_D(cell_d_4_a_d), .Sel_copy(cell_d_4_sel_copy), .B_copy(cell_d_4_b_copy));
  Cell_D cell_d_5 (
    .Sel(cell_d_3_sel_copy), .A(cell_d_4_a_d), .B(cell_d_2_b_copy), .Bin(cell_d_8_bout),
    .Bout(cell_d_5_bout), .A_D(cell_d_5_a_d), .Sel_copy(cell_d_5_sel_copy), .B_copy(cell_d_5_b_copy));
  Cell_D cell_d_6 (
    .Sel(cell_d_6_bout), .A(cell_d_5_a_d), .B(cell_d_3_b_copy), .Bin(cell_d_9_bout), .Bout(cell_d_6_bout),
    .Sel_copy(cell_d_6_sel_copy), .B_copy(cell_d_6_b_copy));  // open: A_D
  Cell_D cell_d_7 (
    .Sel(cell_d_4_sel_copy), .A(A[3]), .B(B[0]), .Bin(1'b0), .Bout(cell_d_7_bout), .A_D(cell_d_7_a_d),
    .B_copy(cell_d_7_b_copy));  // open: Sel_copy
  Cell_D cell_d_8 (
    .Sel(cell_d_5_sel_copy), .A(cell_d_7_a_d), .B(cell_d_4_b_copy), .Bin(cell_d_11_bout),
    .Bout(cell_d_8_bout), .A_D(cell_d_8_a_d), .Sel_copy(cell_d_8_sel_copy), .B_copy(cell_d_8_b_copy));
  Cell_D cell_d_9 (
    .Sel(cell_d_6_sel_copy), .A(cell_d_8_a_d), .B(cell_d_5_b_copy), .Bin(cell_d_12_bout),
    .Bout(cell_d_9_bout), .A_D(cell_d_9_a_d), .Sel_copy(cell_d_9_sel_copy), .B_copy(cell_d_9_b_copy));
  Cell_D cell_d_10 (
    .Sel(cell_d_10_bout), .A(cell_d_9_a_d), .B(cell_d_6_b_copy), .Bin(cell_d_13_bout), .Bout(cell_d_10_bout),
    .Sel_copy(cell_d_10_sel_copy));  // open: A_D, B_copy
  Cell_D cell_d_11 (
    .Sel(cell_d_8_sel_copy), .A(A[2]), .B(cell_d_7_b_copy), .Bin(1'b0), .Bout(cell_d_11_bout),
    .A_D(cell_d_11_a_d), .B_copy(cell_d_11_b_copy));  // open: Sel_copy
  Cell_D cell_d_12 (
    .Sel(cell_d_9_sel_copy), .A(cell_d_11_a_d), .B(cell_d_8_b_copy), .Bin(cell_d_14_bout),
    .Bout(cell_d_12_bout), .A_D(cell_d_12_a_d), .Sel_copy(cell_d_12_sel_copy), .B_copy(cell_d_12_b_copy));
  Cell_D cell_d_13 (
    .Sel(cell_d_10_sel_copy), .A(cell_d_12_a_d), .B(cell_d_9_b_copy), .Bin(cell_d_15_bout),
    .Bout(cell_d_13_bout), .Sel_copy(cell_d_13_sel_copy));  // open: A_D, B_copy
  Cell_D cell_d_14 (
    .Sel(cell_d_12_sel_copy), .A(A[1]), .B(cell_d_11_b_copy), .Bin(1'b0), .Bout(cell_d_14_bout),
    .A_D(cell_d_14_a_d), .B_copy(cell_d_14_b_copy));  // open: Sel_copy
  Cell_D cell_d_15 (
    .Sel(cell_d_13_sel_copy), .A(cell_d_14_a_d), .B(cell_d_12_b_copy), .Bin(cell_d_16_bout),
    .Bout(cell_d_15_bout), .Sel_copy(cell_d_15_sel_copy));  // open: A_D, B_copy
  Cell_D cell_d_16 (
    .Sel(cell_d_15_sel_copy), .A(A[0]), .B(cell_d_14_b_copy), .Bin(1'b0), .Bout(cell_d_16_bout));  // open: A_D, Sel_copy, B_copy
  nor nor_1 (Exception, B[0], B[1], B[2], B[3]);

  // Notes on the sheet:
  //   4 bit Unsigned Divider Circuit
endmodule

module ALU_4 (
  input  [3:0] A_4bit,
  input  [3:0] B_4bit,
  input  [3:0] Op,
  output [3:0] R_4bit,
  output SF,
  output ZF,
  output CF,
  output MUL_EXCP,
  output DIV_EXCP
);

  wire [3:0] ADDSUB4, AND4, L_ROTATE4, L_Shift4, NOT4, OR4, R_ROTATE4, R_Shift4, UDIV4, UMUL4, XOR4;

  AND_Gate_4bit and_gate_4bit_1 (.A(A_4bit), .B(B_4bit), .O(AND4));
  OR_Gate_4bit or_gate_4bit_1 (.A(A_4bit), .B(B_4bit), .O(OR4));
  XOR_Gate xor_gate_1 (.A(A_4bit), .B(B_4bit), .O(XOR4));
  Left_Shifter_4bit left_shifter_4bit_1 (.A(A_4bit), .Shift(B_4bit[1:0]), .O(L_Shift4));
  Right_Shifter_4bit right_shifter_4bit_1 (.A(A_4bit), .Shift(B_4bit[1:0]), .O(R_Shift4));
  Adder_Subtractor_4bit adder_subtractor_4bit_1 (.A(A_4bit), .B(B_4bit), .Sel(Op[1]), .O(ADDSUB4), .Carry(CF));
  Unsigned_Multiplier_4bit unsigned_multiplier_4bit_1 (.B(B_4bit), .A(A_4bit), .OverFlow(MUL_EXCP), .O(UMUL4));
  Left_Rotate_4bit left_rotate_4bit_1 (.A(A_4bit), .Shift(B_4bit[1:0]), .O(L_ROTATE4));
  Right_Rotate_4bit right_rotate_4bit_1 (.A(A_4bit), .Shift(B_4bit[1:0]), .O(R_ROTATE4));
  NOT_Gate_4bit not_gate_4bit_1 (.A(A_4bit), .O(NOT4));
  Unsigned_divider_4bit unsigned_divider_4bit_1 (.B(B_4bit), .A(A_4bit), .Exception(DIV_EXCP), .O(UDIV4));
  Multiplexer #(.select(4), .width(4)) multiplexer_1 (
    .in0(AND4), .in1(OR4), .in2(XOR4), .in3(L_Shift4), .in4(R_Shift4), .in5(ADDSUB4), .in6(UMUL4),
    .in7(L_ROTATE4), .in8(R_ROTATE4), .in9(NOT4), .in10(UDIV4), .out(R_4bit), .sel(Op));  // open: in11, in12, in13, in14, in15
  nor nor_1 (ZF, R_4bit[0], R_4bit[1], R_4bit[2], R_4bit[3]);

  assign SF = R_4bit[3];

  // Other names for the same wires on the sheet: A[3:0] = A_4bit; B[3:0] = B_4bit; Shift[1:0] = B_4bit[1:0];
  //   Sel_Add_Sub = Op[1]

  // Notes on the sheet:
  //   4 bit ALU
endmodule

module ALU_Testing (
  input  [3:0] A,
  input  [3:0] B,
  input  [3:0] OP,
  output [3:0] R,
  output DIV_Exception,
  output MUL_Exception,
  output CF,
  output SF,
  output ZF
);

  ALU_4 alu_4_1 (
    .B_4bit(B), .A_4bit(A), .Op(OP), .R_4bit(R), .SF(SF), .ZF(ZF), .CF(CF), .MUL_EXCP(MUL_Exception),
    .DIV_EXCP(DIV_Exception));

  // Notes on the sheet:
  //   Complete 4 bit ALU
endmodule
