// Logisim project CPU_prac1.circ as structural Verilog: 14 circuits, main circuit ALU_Adder1bit
module ALU_Adder1bit (
  input  a,
  input  b,
  input  Cin,
  output S,
  output Cout
);

  wire and_1_out, and_2_out, xor_1_out;

  xor xor_1 (xor_1_out, a, b);
  and and_1 (and_1_out, b, a);
  xor xor_2 (S, xor_1_out, Cin);
  and and_2 (and_2_out, Cin, xor_1_out);
  or or_1 (Cout, and_2_out, and_1_out);
endmodule

module ALU_Adder3bit (
  input  [2:0] A,
  input  Sel,
  input  [2:0] B,
  output Carry,
  output [2:0] O
);

  wire alu_adder1bit_2_cout, alu_adder1bit_3_cout, xor_1_out, xor_2_out, xor_3_out;

  xor xor_1 (xor_1_out, B[2], Sel);
  ALU_Adder1bit alu_adder1bit_1 (.a(A[2]), .b(xor_1_out), .Cin(alu_adder1bit_2_cout), .S(O[2]), .Cout(Carry));
  xor xor_2 (xor_2_out, B[1], Sel);
  ALU_Adder1bit alu_adder1bit_2 (
    .a(A[1]), .b(xor_2_out), .Cin(alu_adder1bit_3_cout), .S(O[1]), .Cout(alu_adder1bit_2_cout));
  xor xor_3 (xor_3_out, B[0], Sel);
  ALU_Adder1bit alu_adder1bit_3 (.a(A[0]), .b(xor_3_out), .Cin(Sel), .S(O[0]), .Cout(alu_adder1bit_3_cout));
endmodule

module ALU_LeftShift3bit (
  input  [2:0] A,
  input  [1:0] Shift,
  output [2:0] O
);

  Multiplexer #(.select(2)) multiplexer_1 (.in0(A[2]), .in1(A[1]), .in2(A[0]), .in3(1'b0), .out(O[2]), .sel(Shift));
  Multiplexer #(.select(2)) multiplexer_2 (.in0(A[1]), .in1(A[0]), .in2(1'b0), .in3(1'b0), .out(O[1]), .sel(Shift));
  Multiplexer #(.select(2)) multiplexer_3 (.in0(A[0]), .in1(1'b0), .in2(1'b0), .in3(1'b0), .out(O[0]), .sel(Shift));
endmodule

module ALU3bit (
  input  [2:0] A,
  input  [2:0] B,
  input  [1:0] OP,
  output ZF,
  output [2:0] R,
  output SF,
  output CF
);

  wire [2:0] ADD, SHL;

  ALU_Adder3bit alu_adder3bit_1 (.A(A), .B(B), .Sel(OP[0]), .O(ADD), .Carry(CF));
  ALU_LeftShift3bit alu_leftshift3bit_1 (.A(A), .Shift(B[1:0]), .O(SHL));
  Multiplexer #(.select(2), .width(3)) multiplexer_1 (.in0(ADD), .in1(ADD), .in2(SHL), .out(R), .sel(OP));  // open: in3
  nor nor_1 (ZF, R[0], R[1], R[2]);

  assign SF = R[2];

  // Other names for the same wires on the sheet: Shift[1:0] = B[1:0]; Sel = OP[0]
endmodule

module RF_1bit (
  input  Din,
  input  Sel,
  input  CLK,
  output Dout
);

  wire multiplexer_1_out;

  Multiplexer multiplexer_1 (.in0(Dout), .in1(Din), .out(multiplexer_1_out), .sel(Sel));
  D_Flip_Flop d_ff_1 (.D(multiplexer_1_out), .clk(CLK), .Q(Dout));  // open: Qn, preset, reset
endmodule

module RF_3bit (
  input  [2:0] Din,
  input  Sel,
  input  CLK,
  output [2:0] Dout
);

  RF_1bit rf_1bit_1 (.Din(Din[0]), .Sel(Sel), .CLK(CLK), .Dout(Dout[0]));
  RF_1bit rf_1bit_2 (.Din(Din[1]), .Sel(Sel), .CLK(CLK), .Dout(Dout[1]));
  RF_1bit rf_1bit_3 (.Din(Din[2]), .Sel(Sel), .CLK(CLK), .Dout(Dout[2]));
endmodule

module RF_Set (
  input  [2:0] WRD,
  input  [1:0] RA,
  input  REG_EN,
  input  [1:0] WR,
  input  [2:0] InD,
  input  InE,
  input  [1:0] RB,
  input  CLK,
  output [2:0] A,
  output [2:0] R0,
  output [2:0] R1,
  output [2:0] R2,
  output [2:0] R3,
  output [2:0] OutD,
  output [2:0] B
);

  wire decoder_1_out0, decoder_1_out1, decoder_1_out3;

  Decoder #(.select(2)) decoder_1 (
    .out0(decoder_1_out0), .out1(decoder_1_out1), .out3(decoder_1_out3), .sel(WR), .en(REG_EN));  // open: out2
  RF_3bit rf_3bit_1 (.Din(WRD), .CLK(CLK), .Sel(decoder_1_out0), .Dout(R0));
  RF_3bit rf_3bit_2 (.Din(WRD), .CLK(CLK), .Sel(decoder_1_out1), .Dout(R1));
  RF_3bit rf_3bit_3 (.Din(InD), .CLK(CLK), .Sel(InE), .Dout(R2));
  RF_3bit rf_3bit_4 (.Din(WRD), .CLK(CLK), .Sel(decoder_1_out3), .Dout(OutD));
  Multiplexer #(.select(2), .width(3)) multiplexer_1 (.in0(R0), .in1(R1), .in2(R2), .in3(OutD), .out(A), .sel(RA));
  Multiplexer #(.select(2), .width(3)) multiplexer_2 (.in0(R0), .in1(R1), .in2(R2), .in3(OutD), .out(B), .sel(RB));

  assign R3 = OutD;
endmodule

module RAM1X1 (
  input  RS1,
  input  WD,
  input  WS,
  input  CLK,
  input  RS2,
  output RD1,
  output RD2,
  output Data
);

  wire multiplexer_1_out;

  Multiplexer multiplexer_1 (.in0(Data), .in1(WD), .out(multiplexer_1_out), .sel(WS));
  D_Flip_Flop d_ff_1 (.D(multiplexer_1_out), .clk(CLK), .Q(Data));  // open: Qn, preset, reset
  and and_1 (RD1, RS1, Data);
  and and_2 (RD2, Data, RS2);
endmodule

module RAM1X9 (
  input  RS1,
  input  RS2,
  input  WS,
  input  CLK,
  input  [8:0] WD,
  output [8:0] RD1,
  output [8:0] D,
  output [8:0] RD2
);

  RAM1X1 ram1x1_1 (.WD(WD[8]), .WS(WS), .CLK(CLK), .RS1(RS1), .RS2(RS2), .Data(D[8]), .RD1(RD1[8]), .RD2(RD2[8]));
  RAM1X1 ram1x1_2 (.WD(WD[5]), .WS(WS), .CLK(CLK), .RS1(RS1), .RS2(RS2), .Data(D[5]), .RD1(RD1[5]), .RD2(RD2[5]));
  RAM1X1 ram1x1_3 (.WD(WD[2]), .WS(WS), .CLK(CLK), .RS1(RS1), .RS2(RS2), .Data(D[2]), .RD1(RD1[2]), .RD2(RD2[2]));
  RAM1X1 ram1x1_4 (.WD(WD[7]), .WS(WS), .CLK(CLK), .RS1(RS1), .RS2(RS2), .Data(D[7]), .RD1(RD1[7]), .RD2(RD2[7]));
  RAM1X1 ram1x1_5 (.WD(WD[4]), .WS(WS), .CLK(CLK), .RS1(RS1), .RS2(RS2), .Data(D[4]), .RD1(RD1[4]), .RD2(RD2[4]));
  RAM1X1 ram1x1_6 (.WD(WD[1]), .WS(WS), .CLK(CLK), .RS1(RS1), .RS2(RS2), .Data(D[1]), .RD1(RD1[1]), .RD2(RD2[1]));
  RAM1X1 ram1x1_7 (.WD(WD[6]), .WS(WS), .CLK(CLK), .RS1(RS1), .RS2(RS2), .Data(D[6]), .RD1(RD1[6]), .RD2(RD2[6]));
  RAM1X1 ram1x1_8 (.WD(WD[3]), .WS(WS), .CLK(CLK), .RS1(RS1), .RS2(RS2), .Data(D[3]), .RD1(RD1[3]), .RD2(RD2[3]));
  RAM1X1 ram1x1_9 (.WD(WD[0]), .WS(WS), .CLK(CLK), .RS1(RS1), .RS2(RS2), .Data(D[0]), .RD1(RD1[0]), .RD2(RD2[0]));

  // Other names for the same wires on the sheet: R1_0 = RD1[0]; R1_1 = RD1[1]; R1_2 = RD1[2]; R1_3 = RD1[3];
  //   R1_4 = RD1[4]; R1_5 = RD1[5]; R1_6 = RD1[6]; R1_7 = RD1[7]; R1_8 = RD1[8]; R2_0 = RD2[0]; R2_1 = RD2[1];
  //   R2_2 = RD2[2]; R2_3 = RD2[3]; R2_4 = RD2[4]; R2_5 = RD2[5]; R2_6 = RD2[6]; R2_7 = RD2[7]; R2_8 = RD2[8]
endmodule

module RAM8X9 (
  input  [2:0] RA1,
  input  [2:0] RA2,
  input  WE,
  input  [2:0] WA,
  input  CLK,
  input  [8:0] WD,
  output [8:0] RD1,
  output [8:0] RD2,
  output [8:0] D0,
  output [8:0] D1,
  output [8:0] D2,
  output [8:0] D3,
  output [8:0] D4,
  output [8:0] D5,
  output [8:0] D6,
  output [8:0] D7
);

  wire RS1_0, RS1_1, RS1_2, RS1_3, RS1_4, RS1_5, RS1_6, RS1_7, RS2_0, RS2_1, RS2_2, RS2_3, RS2_4, RS2_5,
       RS2_6, RS2_7, W0, W1, W2, W3, W4, W5, W6, W7;
  wire [8:0] RD1_0, RD1_1, RD1_2, RD1_3, RD1_4, RD1_5, RD1_6, RD1_7, RD2_0, RD2_1, RD2_2, RD2_3, RD2_4,
       RD2_5, RD2_6, RD2_7;

  Decoder #(.select(3)) decoder_1 (
    .out0(RS1_0), .out1(RS1_1), .out2(RS1_2), .out3(RS1_3), .out4(RS1_4), .out5(RS1_5), .out6(RS1_6),
    .out7(RS1_7), .sel(RA1));  // open: en
  Decoder #(.select(3)) decoder_2 (
    .out0(RS2_0), .out1(RS2_1), .out2(RS2_2), .out3(RS2_3), .out4(RS2_4), .out5(RS2_5), .out6(RS2_6),
    .out7(RS2_7), .sel(RA2));  // open: en
  Decoder #(.select(3)) decoder_3 (
    .out0(W0), .out1(W1), .out2(W2), .out3(W3), .out4(W4), .out5(W5), .out6(W6), .out7(W7), .sel(WA), .en(WE));
  RAM1X9 ram1x9_1 (.RS2(RS2_0), .WS(W0), .CLK(CLK), .WD(WD), .RS1(RS1_0), .RD1(RD1_0), .RD2(RD2_0), .D(D0));
  RAM1X9 ram1x9_2 (.RS2(RS2_1), .WS(W1), .CLK(CLK), .WD(WD), .RS1(RS1_1), .RD1(RD1_1), .RD2(RD2_1), .D(D1));
  RAM1X9 ram1x9_3 (.RS2(RS2_2), .WS(W2), .CLK(CLK), .WD(WD), .RS1(RS1_2), .RD1(RD1_2), .RD2(RD2_2), .D(D2));
  RAM1X9 ram1x9_4 (.RS2(RS2_3), .WS(W3), .CLK(CLK), .WD(WD), .RS1(RS1_3), .RD1(RD1_3), .RD2(RD2_3), .D(D3));
  RAM1X9 ram1x9_5 (.RS2(RS2_4), .WS(W4), .CLK(CLK), .WD(WD), .RS1(RS1_4), .RD1(RD1_4), .RD2(RD2_4), .D(D4));
  RAM1X9 ram1x9_6 (.RS2(RS2_5), .WS(W5), .CLK(CLK), .WD(WD), .RS1(RS1_5), .RD1(RD1_5), .RD2(RD2_5), .D(D5));
  RAM1X9 ram1x9_7 (.RS2(RS2_6), .WS(W6), .CLK(CLK), .WD(WD), .RS1(RS1_6), .RD1(RD1_6), .RD2(RD2_6), .D(D6));
  RAM1X9 ram1x9_8 (.RS2(RS2_7), .WS(W7), .CLK(CLK), .WD(WD), .RS1(RS1_7), .RD1(RD1_7), .RD2(RD2_7), .D(D7));
  assign RD1 = RD1_0 | RD1_1 | RD1_2 | RD1_3 | RD1_4 | RD1_5 | RD1_6 | RD1_7;  // OR_Gate or_1, 9 bits wide
  assign RD2 = RD2_0 | RD2_1 | RD2_2 | RD2_3 | RD2_4 | RD2_5 | RD2_6 | RD2_7;  // OR_Gate or_2, 9 bits wide
endmodule

module PC (
  input  [2:0] I,
  input  CLK,
  output [2:0] O
);

  D_Flip_Flop d_ff_1 (.D(I[0]), .clk(CLK), .Q(O[0]));  // open: Qn, preset, reset
  D_Flip_Flop d_ff_2 (.D(I[1]), .clk(CLK), .Q(O[1]));  // open: Qn, preset, reset
  D_Flip_Flop d_ff_3 (.D(I[2]), .clk(CLK), .Q(O[2]));  // open: Qn, preset, reset
endmodule

module CU (
  input  [3:0] Opcode,
  input  ZF,
  input  SF,
  input  CF,
  output Imm_Sel,
  output REG_EN,
  output [1:0] OP,
  output JMP_SEL,
  output ST_SEL
);

  wire and_1_out, CMP_out, Flag_out, JEop_out, JMP_out, Mem_out, or_1_out, or_2_out, RegM_out, StOp_out;

  and JMP (JMP_out, ~Opcode[3], Opcode[2]);  // AND_Gate
  and JEop (JEop_out, ~Opcode[1], ~Opcode[0]);  // AND_Gate
  and Flag (Flag_out, ZF, ~SF);  // AND_Gate
  and Mem (Mem_out, Opcode[3], ~Opcode[2]);  // AND_Gate
  and StOp (StOp_out, ~Opcode[1], ~Opcode[0]);  // AND_Gate
  and ImmM (Imm_Sel, ~Opcode[3], ~Opcode[2]);  // AND_Gate
  and RegM (RegM_out, Opcode[3], Opcode[2]);
  and CMP (CMP_out, ~Opcode[1], Opcode[0]);  // AND_Gate
  and JE (JMP_SEL, JMP_out, JEop_out, Flag_out);
  and ST (ST_SEL, Mem_out, StOp_out);
  or or_1 (or_1_out, Imm_Sel, RegM_out);
  and and_1 (and_1_out, or_1_out, CMP_out);
  or or_2 (or_2_out, and_1_out, JMP_out, ST_SEL);
  not not_1 (REG_EN, or_2_out);

  assign OP = Opcode[1:0];
endmodule

module FLAG_REG (
  input  ZF,
  input  SF,
  input  CF,
  input  CLK,
  output dZF,
  output dSF,
  output dCF
);

  D_Flip_Flop d_ff_1 (.D(ZF), .clk(CLK), .Q(dZF));  // open: Qn, preset, reset
  D_Flip_Flop d_ff_2 (.D(SF), .clk(CLK), .Q(dSF));  // open: Qn, preset, reset
  D_Flip_Flop d_ff_3 (.D(CF), .clk(CLK), .Q(dCF));  // open: Qn, preset, reset
endmodule

module CPU_3bit (
  input  [8:0] WD,
  input  [2:0] WA,
  input  InE,
  input  WE,
  input  CLK,
  input  PC_Enable,
  output [8:0] RAM4,
  output [8:0] RAM0,
  output [8:0] RAM5,
  output [8:0] RAM1,
  output [2:0] REG0,
  output [8:0] RAM6,
  output [8:0] RAM2,
  output [2:0] REG1,
  output [2:0] REG2,
  output [8:0] RAN7,
  output [8:0] RAM3,
  output [2:0] REG3
);

  wire alu3bit_1_cf, alu3bit_1_sf, alu3bit_1_zf, CF, CPU_CLK, IMM_SEL, JMP_SEL, multiplexer_4_out, REG_EN,
       SF, ST_SEL, ZF;
  wire [1:0] OP;
  wire [2:0] adder_1_out, alu3bit_1_r, InD, JMP_ADR, multiplexer_1_out, multiplexer_3_out, multiplexer_5_out,
       OutD, pc_1_o, ST_ADR, ST_DATA;
  wire [8:0] bit_extender_1_out, multiplexer_2_out;
  wire [8:3] ram8x9_1_rd1;

  assign bit_extender_1_out = {{6{1'b0}}, ST_DATA};  // Bit_Extender bit_extender_1
  Multiplexer #(.width(3)) multiplexer_1 (.in0(adder_1_out), .in1(JMP_ADR), .out(multiplexer_1_out), .sel(JMP_SEL));
  Multiplexer #(.width(9)) multiplexer_2 (.in0(WD), .in1(bit_extender_1_out), .out(multiplexer_2_out), .sel(ST_SEL));
  Multiplexer #(.width(3)) multiplexer_3 (.in0(WA), .in1(ST_ADR), .out(multiplexer_3_out), .sel(ST_SEL));
  Multiplexer multiplexer_4 (.in0(WE), .in1(ST_SEL), .out(multiplexer_4_out), .sel(ST_SEL));
  Adder #(.width(3)) adder_1 (.a(pc_1_o), .b(3'b001), .out(adder_1_out));  // open: cin, cout
  PC pc_1 (.I(multiplexer_1_out), .CLK(CPU_CLK), .O(pc_1_o));
  and and_1 (CPU_CLK, CLK, PC_Enable);
  DipSwitch #(.number(3)) dipswitch_1 (.sw1(InD[2]), .sw2(InD[1]), .sw3(InD[0]));
  LED led_1 (.in(OutD[2]));
  LED led_2 (.in(OutD[1]));
  RAM8X9 ram8x9_1 (
    .WD(multiplexer_2_out), .WE(multiplexer_4_out), .CLK(CLK), .RA1(pc_1_o), .WA(multiplexer_3_out),
    .D0(RAM0), .D1(RAM1), .D2(RAM2), .D3(RAM3), .D4(RAM4), .D5(RAM5), .D6(RAM6), .D7(RAN7),
    .RD1({ram8x9_1_rd1, JMP_ADR}));  // open: RA2, RD2
  LED led_3 (.in(OutD[0]));
  FLAG_REG flag_reg_1 (
    .CLK(CPU_CLK), .ZF(alu3bit_1_cf), .SF(alu3bit_1_sf), .CF(alu3bit_1_zf), .dZF(ZF), .dSF(SF), .dCF(CF));
  CU cu_1 (
    .Opcode(ram8x9_1_rd1[8:5]), .ZF(ZF), .SF(SF), .CF(CF), .REG_EN(REG_EN), .OP(OP), .JMP_SEL(JMP_SEL),
    .Imm_Sel(IMM_SEL), .ST_SEL(ST_SEL));
  RF_Set rf_set_1 (
    .REG_EN(REG_EN), .WR(ram8x9_1_rd1[4:3]), .InD(InD), .InE(InE), .CLK(CPU_CLK), .WRD(alu3bit_1_r),
    .RA(ram8x9_1_rd1[4:3]), .RB(JMP_ADR[2:1]), .A(ST_ADR), .R0(REG0), .R1(REG1), .R2(REG2), .R3(REG3),
    .OutD(OutD), .B(ST_DATA));
  Multiplexer #(.width(3)) multiplexer_5 (.in0(ST_DATA), .in1(JMP_ADR), .out(multiplexer_5_out), .sel(IMM_SEL));
  ALU3bit alu3bit_1 (
    .A(ST_ADR), .B(multiplexer_5_out), .OP(OP), .R(alu3bit_1_r), .ZF(alu3bit_1_zf), .SF(alu3bit_1_sf),
    .CF(alu3bit_1_cf));

  // Other names for the same wires on the sheet: D0[8:0] = RAM0; D1[8:0] = RAM1; D2[8:0] = RAM2; D3[8:0] = RAM3;
  //   D4[8:0] = RAM4; D5[8:0] = RAM5; D6[8:0] = RAM6; D7[8:0] = RAN7; R0[2:0] = REG0; R1[2:0] = REG1; R2[2:0] = REG2;
  //   R3[2:0] = REG3
endmodule
