// Logisim project CPU_prac2.circ as structural Verilog: 14 circuits, main circuit ALU_Adder
module ALU_Adder (
  input  [4:0] A,
  input  Sel,
  input  [4:0] B,
  output Carry,
  output [4:0] O
);

  wire alu_1bit_adder_2_cout, alu_1bit_adder_3_cout, alu_1bit_adder_4_cout, alu_1bit_adder_5_cout, xor_1_out,
       xor_2_out, xor_3_out, xor_4_out, xor_5_out;

  xor xor_1 (xor_1_out, B[4], Sel);
  ALU_1bit_Adder alu_1bit_adder_1 (.a(A[4]), .b(xor_1_out), .Cin(alu_1bit_adder_2_cout), .S(O[4]), .Cout(Carry));
  xor xor_2 (xor_2_out, B[3], Sel);
  ALU_1bit_Adder alu_1bit_adder_2 (
    .a(A[3]), .b(xor_2_out), .Cin(alu_1bit_adder_3_cout), .S(O[3]), .Cout(alu_1bit_adder_2_cout));
  xor xor_3 (xor_3_out, B[2], Sel);
  ALU_1bit_Adder alu_1bit_adder_3 (
    .a(A[2]), .b(xor_3_out), .Cin(alu_1bit_adder_4_cout), .S(O[2]), .Cout(alu_1bit_adder_3_cout));
  xor xor_4 (xor_4_out, B[1], Sel);
  ALU_1bit_Adder alu_1bit_adder_4 (
    .a(A[1]), .b(xor_4_out), .Cin(alu_1bit_adder_5_cout), .S(O[1]), .Cout(alu_1bit_adder_4_cout));
  xor xor_5 (xor_5_out, B[0], Sel);
  ALU_1bit_Adder alu_1bit_adder_5 (.a(A[0]), .b(xor_5_out), .Cin(Sel), .S(O[0]), .Cout(alu_1bit_adder_5_cout));
endmodule

module ALU_SHR (
  input  [4:0] A,
  input  [1:0] Shift,
  output [4:0] O
);

  Multiplexer #(.select(2)) multiplexer_1 (.in0(A[4]), .in1(1'b0), .in2(1'b0), .in3(1'b0), .out(O[4]), .sel(Shift));
  Multiplexer #(.select(2)) multiplexer_2 (.in0(A[3]), .in1(A[4]), .in2(1'b0), .in3(1'b0), .out(O[3]), .sel(Shift));
  Multiplexer #(.select(2)) multiplexer_3 (.in0(A[2]), .in1(A[3]), .in2(A[4]), .in3(1'b0), .out(O[2]), .sel(Shift));
  Multiplexer #(.select(2)) multiplexer_4 (.in0(A[1]), .in1(A[2]), .in2(A[3]), .in3(A[4]), .out(O[1]), .sel(Shift));
  Multiplexer #(.select(2)) multiplexer_5 (.in0(A[0]), .in1(A[1]), .in2(A[2]), .in3(A[3]), .out(O[0]), .sel(Shift));
endmodule

module ALU_5bit (
  input  [4:0] A,
  input  [4:0] B,
  input  [1:0] Op,
  output ZF,
  output [4:0] R,
  output SF,
  output CF
);

  wire [4:0] Add, SHR;

  ALU_Adder alu_adder_1 (.A(A), .B(B), .Sel(Op[0]), .O(Add), .Carry(CF));
  ALU_SHR alu_shr_1 (.A(A), .Shift(B[1:0]), .O(SHR));
  Multiplexer #(.select(2), .width(5)) multiplexer_1 (.in0(SHR), .in1(Add), .in2(Add), .out(R), .sel(Op));  // open: in3
  nor nor_1 (ZF, R[0], R[1], R[2], R[3], R[4]);

  assign SF = R[4];

  // Other names for the same wires on the sheet: Shift[1:0] = B[1:0]; Sel = Op[0]
endmodule

module Reg_1X5 (
  input  [4:0] Din,
  input  Sel,
  input  CLK,
  output [4:0] Dout
);

  Reg_1X1 reg_1x1_1 (.Din(Din[0]), .Sel(Sel), .CLK(CLK), .Dout(Dout[0]));
  Reg_1X1 reg_1x1_2 (.Din(Din[1]), .Sel(Sel), .CLK(CLK), .Dout(Dout[1]));
  Reg_1X1 reg_1x1_3 (.Din(Din[2]), .Sel(Sel), .CLK(CLK), .Dout(Dout[2]));
  Reg_1X1 reg_1x1_4 (.Din(Din[3]), .Sel(Sel), .CLK(CLK), .Dout(Dout[3]));
  Reg_1X1 reg_1x1_5 (.Din(Din[4]), .Sel(Sel), .CLK(CLK), .Dout(Dout[4]));
endmodule

module Reg_4X5 (
  input  [4:0] Wrd,
  input  [1:0] Ra,
  input  REG_EN,
  input  [1:0] Wr,
  input  [4:0] InD,
  input  InE,
  input  CLK,
  input  [1:0] Rb,
  output [4:0] A,
  output [4:0] R0,
  output [4:0] R1,
  output [4:0] R2,
  output [4:0] R3,
  output [4:0] OutD,
  output [4:0] B
);

  wire decoder_1_out0, decoder_1_out1, decoder_1_out3;

  Decoder #(.select(2)) decoder_1 (
    .out0(decoder_1_out0), .out1(decoder_1_out1), .out3(decoder_1_out3), .sel(Wr), .en(REG_EN));  // open: out2
  Reg_1X5 reg_1x5_1 (.Sel(decoder_1_out0), .CLK(CLK), .Din(Wrd), .Dout(R0));
  Reg_1X5 reg_1x5_2 (.Sel(decoder_1_out1), .CLK(CLK), .Din(Wrd), .Dout(R1));
  Reg_1X5 reg_1x5_3 (.Sel(InE), .CLK(CLK), .Din(InD), .Dout(R2));
  Reg_1X5 reg_1x5_4 (.Sel(decoder_1_out3), .CLK(CLK), .Din(Wrd), .Dout(OutD));
  Multiplexer #(.select(2), .width(5)) multiplexer_1 (.in0(R0), .in1(R1), .in2(R2), .in3(OutD), .out(A), .sel(Ra));
  Multiplexer #(.select(2), .width(5)) multiplexer_2 (.in0(R0), .in1(R1), .in2(R2), .in3(OutD), .out(B), .sel(Rb));

  assign R3 = OutD;
endmodule

module RAM_1X11 (
  input  RS1,
  input  RS2,
  input  WS,
  input  CLK,
  input  [10:0] WD,
  output [10:0] RD1,
  output [10:0] RD2,
  output [10:0] D
);

  RAM1bit ram1bit_1 (.WD(WD[8]), .WS(WS), .CLK(CLK), .RS1(RS1), .RS2(RS2), .Data(D[8]), .RD1(RD1[8]), .RD2(RD2[8]));
  RAM1bit ram1bit_2 (.WD(WD[5]), .WS(WS), .CLK(CLK), .RS1(RS1), .RS2(RS2), .Data(D[5]), .RD1(RD1[5]), .RD2(RD2[5]));
  RAM1bit ram1bit_3 (.WD(WD[2]), .WS(WS), .CLK(CLK), .RS1(RS1), .RS2(RS2), .Data(D[2]), .RD1(RD1[2]), .RD2(RD2[2]));
  RAM1bit ram1bit_4 (.WD(WD[10]), .WS(WS), .CLK(CLK), .RS1(RS1), .RS2(RS2), .Data(D[10]), .RD1(RD1[10]), .RD2(RD2[10]));
  RAM1bit ram1bit_5 (.WD(WD[7]), .WS(WS), .CLK(CLK), .RS1(RS1), .RS2(RS2), .Data(D[7]), .RD1(RD1[7]), .RD2(RD2[7]));
  RAM1bit ram1bit_6 (.WD(WD[4]), .WS(WS), .CLK(CLK), .RS1(RS1), .RS2(RS2), .Data(D[4]), .RD1(RD1[4]), .RD2(RD2[4]));
  RAM1bit ram1bit_7 (.WD(WD[1]), .WS(WS), .CLK(CLK), .RS1(RS1), .RS2(RS2), .Data(D[1]), .RD1(RD1[1]), .RD2(RD2[1]));
  RAM1bit ram1bit_8 (.WD(WD[9]), .WS(WS), .CLK(CLK), .RS1(RS1), .RS2(RS2), .Data(D[9]), .RD1(RD1[9]), .RD2(RD2[9]));
  RAM1bit ram1bit_9 (.WD(WD[6]), .WS(WS), .CLK(CLK), .RS1(RS1), .RS2(RS2), .Data(D[6]), .RD1(RD1[6]), .RD2(RD2[6]));
  RAM1bit ram1bit_10 (.WD(WD[3]), .WS(WS), .CLK(CLK), .RS1(RS1), .RS2(RS2), .Data(D[3]), .RD1(RD1[3]), .RD2(RD2[3]));
  RAM1bit ram1bit_11 (.WD(WD[0]), .WS(WS), .CLK(CLK), .RS1(RS1), .RS2(RS2), .Data(D[0]), .RD1(RD1[0]), .RD2(RD2[0]));

  // Other names for the same wires on the sheet: R1_0 = RD1[0]; R1_1 = RD1[1]; R1_2 = RD1[2]; R1_3 = RD1[3];
  //   R1_4 = RD1[4]; R1_5 = RD1[5]; R1_6 = RD1[6]; R1_7 = RD1[7]; R1_8 = RD1[8]; R1_9 = RD1[9]; R1_10 = RD1[10];
  //   R2_0 = RD2[0]; R2_1 = RD2[1]; R2_2 = RD2[2]; R2_3 = RD2[3]; R2_4 = RD2[4]; R2_5 = RD2[5]; R2_6 = RD2[6];
  //   R2_7 = RD2[7]; R2_8 = RD2[8]; R2_9 = RD2[9]; R2_10 = RD2[10]
endmodule

module RAM_8X11 (
  input  [2:0] RA1,
  input  [2:0] RA2,
  input  WE,
  input  [2:0] WA,
  input  CLK,
  input  [10:0] WD,
  output [10:0] RD1,
  output [10:0] RD2,
  output [10:0] D0,
  output [10:0] D1,
  output [10:0] D2,
  output [10:0] D3,
  output [10:0] D4,
  output [10:0] D5,
  output [10:0] D6,
  output [10:0] D7
);

  wire RS1_0, RS1_1, RS1_2, RS1_3, RS1_4, RS1_5, RS1_6, RS1_7, RS2_0, RS2_1, RS2_2, RS2_3, RS2_4, RS2_5,
       RS2_6, RS2_7, W0, W1, W2, W3, W4, W5, W6, W7;
  wire [10:0] RD1_0, RD1_1, RD1_2, RD1_3, RD1_4, RD1_5, RD1_6, RD1_7, RD2_0, RD2_1, RD2_2, RD2_3, RD2_4,
       RD2_5, RD2_6, RD2_7;

  Decoder #(.select(3)) decoder_1 (
    .out0(RS1_0), .out1(RS1_1), .out2(RS1_2), .out3(RS1_3), .out4(RS1_4), .out5(RS1_5), .out6(RS1_6),
    .out7(RS1_7), .sel(RA1));  // open: en
  Decoder #(.select(3)) decoder_2 (
    .out0(RS2_0), .out1(RS2_1), .out2(RS2_2), .out3(RS2_3), .out4(RS2_4), .out5(RS2_5), .out6(RS2_6),
    .out7(RS2_7), .sel(RA2));  // open: en
  Decoder #(.select(3)) decoder_3 (
    .out0(W0), .out1(W1), .out2(W2), .out3(W3), .out4(W4), .out5(W5), .out6(W6), .out7(W7), .sel(WA), .en(WE));
  RAM_1X11 ram_1x11_1 (.RS2(RS2_0), .WS(W0), .CLK(CLK), .RS1(RS1_0), .WD(WD), .D(D0), .RD1(RD1_0), .RD2(RD2_0));
  RAM_1X11 ram_1x11_2 (.RS2(RS2_1), .WS(W1), .CLK(CLK), .RS1(RS1_1), .WD(WD), .D(D1), .RD1(RD1_1), .RD2(RD2_1));
  RAM_1X11 ram_1x11_3 (.RS2(RS2_2), .WS(W2), .CLK(CLK), .RS1(RS1_2), .WD(WD), .D(D2), .RD1(RD1_2), .RD2(RD2_2));
  RAM_1X11 ram_1x11_4 (.RS2(RS2_3), .WS(W3), .CLK(CLK), .RS1(RS1_3), .WD(WD), .D(D3), .RD1(RD1_3), .RD2(RD2_3));
  RAM_1X11 ram_1x11_5 (.RS2(RS2_4), .WS(W4), .CLK(CLK), .RS1(RS1_4), .WD(WD), .D(D4), .RD1(RD1_4), .RD2(RD2_4));
  RAM_1X11 ram_1x11_6 (.RS2(RS2_5), .WS(W5), .CLK(CLK), .RS1(RS1_5), .WD(WD), .D(D5), .RD1(RD1_5), .RD2(RD2_5));
  RAM_1X11 ram_1x11_7 (.RS2(RS2_6), .WS(W6), .CLK(CLK), .RS1(RS1_6), .WD(WD), .D(D6), .RD1(RD1_6), .RD2(RD2_6));
  RAM_1X11 ram_1x11_8 (.RS2(RS2_7), .WS(W7), .CLK(CLK), .RS1(RS1_7), .WD(WD), .D(D7), .RD1(RD1_7), .RD2(RD2_7));
  assign RD1 = RD1_0 | RD1_1 | RD1_2 | RD1_3 | RD1_4 | RD1_5 | RD1_6 | RD1_7;  // OR_Gate or_1, 11 bits wide
  assign RD2 = RD2_0 | RD2_1 | RD2_2 | RD2_3 | RD2_4 | RD2_5 | RD2_6 | RD2_7;  // OR_Gate or_2, 11 bits wide
endmodule

module CU_5bit (
  input  [3:0] Opcode,
  input  ZF,
  input  SF,
  input  CF,
  output Imm_Sel,
  output REG_EN,
  output [1:0] OP,
  output JMP_SEL,
  output LD_SEL
);

  wire and_1_out, CMP_out, Flag_out, JLop_out, JMP_out, LDOp_out, Mem_out, or_1_out, or_2_out, RegM_out;

  and JMP (JMP_out, Opcode[3], Opcode[2]);
  and JLop (JLop_out, ~Opcode[1], ~Opcode[0]);  // AND_Gate
  and Flag (Flag_out, ~ZF, SF);  // AND_Gate
  and Mem (Mem_out, ~Opcode[3], ~Opcode[2]);  // AND_Gate
  and LDOp (LDOp_out, ~Opcode[1], ~Opcode[0]);  // AND_Gate
  and ImmM (Imm_Sel, Opcode[3], ~Opcode[2]);  // AND_Gate
  and RegM (RegM_out, ~Opcode[3], Opcode[2]);  // AND_Gate
  and CMP (CMP_out, ~Opcode[1], Opcode[0]);  // AND_Gate
  and JE (JMP_SEL, JMP_out, JLop_out, Flag_out);
  and LD (LD_SEL, Mem_out, LDOp_out);
  or or_1 (or_1_out, Imm_Sel, RegM_out);
  and and_1 (and_1_out, or_1_out, CMP_out);
  or or_2 (or_2_out, and_1_out, JMP_out);
  not not_1 (REG_EN, or_2_out);

  assign OP = Opcode[1:0];
endmodule

module PC_5bit (
  input  [2:0] I,
  input  CLK,
  output [2:0] O
);

  D_Flip_Flop d_ff_1 (.D(I[0]), .clk(CLK), .Q(O[0]));  // open: Qn, preset, reset
  D_Flip_Flop d_ff_2 (.D(I[1]), .clk(CLK), .Q(O[1]));  // open: Qn, preset, reset
  D_Flip_Flop d_ff_3 (.D(I[2]), .clk(CLK), .Q(O[2]));  // open: Qn, preset, reset
endmodule

module Flag_regg (
  input  ZF,
  input  SF,
  input  CF,
  input  CLK,
  output dZF,
  output dSF,
  output dCF
);

  D_Flip_Flop d_ff_1 (.D(ZF), .clk(CLK), .Q(dZF));  // open: Qn, preset, reset
  D_Flip_Flop d_ff_2 (.D(SF), .clk(CLK), .Q(dSF));  // open: Qn, preset, reset
  D_Flip_Flop d_ff_3 (.D(CF), .clk(CLK), .Q(dCF));  // open: Qn, preset, reset
endmodule

module Reg_1X1 (
  input  Din,
  input  Sel,
  input  CLK,
  output Dout
);

  wire multiplexer_1_out;

  Multiplexer multiplexer_1 (.in0(Dout), .in1(Din), .out(multiplexer_1_out), .sel(Sel));
  D_Flip_Flop d_ff_1 (.D(multiplexer_1_out), .clk(CLK), .Q(Dout));  // open: Qn, preset, reset
endmodule

module RAM1bit (
  input  RS1,
  input  WD,
  input  WS,
  input  CLK,
  input  RS2,
  output RD1,
  output RD2,
  output Data
);

  wire multiplexer_1_out;

  Multiplexer multiplexer_1 (.in0(Data), .in1(WD), .out(multiplexer_1_out), .sel(WS));
  D_Flip_Flop d_ff_1 (.D(multiplexer_1_out), .clk(CLK), .Q(Data));  // open: Qn, preset, reset
  and and_1 (RD1, RS1, Data);
  and and_2 (RD2, Data, RS2);
endmodule

module CPU_5bit (
  input  [10:0] WD,
  input  [2:0] WA,
  input  WE,
  input  CLK,
  input  [4:0] InD,
  input  PC_Enable,
  input  InE,
  output [4:0] OutD,
  output [10:0] RAM4,
  output [10:0] RAM0,
  output [4:0] REG0,
  output [4:0] REG1,
  output [10:0] RAM5,
  output [10:0] RAM1,
  output [4:0] REG2,
  output [4:0] REG3,
  output [10:0] RAM6,
  output [10:0] RAM2,
  output [10:0] RAM7,
  output [10:0] RAM3
);

  wire alu_5bit_1_cf, alu_5bit_1_sf, alu_5bit_1_zf, CF, CPU_CLK, IMM_SEL, JMP_SEL, LD_SEL, REG_EN, SF, ZF;
  wire [1:0] OP;
  wire [2:0] adder_1_out, JMP_ADR, Ld_Adr, multiplexer_1_out, pc_5bit_1_o;
  wire [4:0] alu_5bit_1_r, LD_data, multiplexer_3_out, reg_4x5_1_a, reg_4x5_1_b;
  wire [4:3] multiplexer_2_out;
  wire [10:0] ram_8x11_1_rd1;
  wire [10:5] ram_8x11_1_rd2;

  Multiplexer #(.width(3)) multiplexer_1 (.in0(adder_1_out), .in1(JMP_ADR), .out(multiplexer_1_out), .sel(JMP_SEL));
  Adder #(.width(3)) adder_1 (.a(pc_5bit_1_o), .b(3'b001), .out(adder_1_out));  // open: cin, cout
  PC_5bit pc_5bit_1 (.I(multiplexer_1_out), .CLK(CPU_CLK), .O(pc_5bit_1_o));
  and and_1 (CPU_CLK, CLK, PC_Enable);
  RAM_8X11 ram_8x11_1 (
    .WE(WE), .CLK(CLK), .RA1(pc_5bit_1_o), .RA2(Ld_Adr), .WA(WA), .WD(WD), .D0(RAM0), .D1(RAM1), .D2(RAM2),
    .D3(RAM3), .D4(RAM4), .D5(RAM5), .D6(RAM6), .D7(RAM7),
    .RD1({ram_8x11_1_rd1[10:7], JMP_ADR, ram_8x11_1_rd1[3:0]}), .RD2({ram_8x11_1_rd2, LD_data}));
  Flag_regg flag_regg_1 (
    .CLK(CPU_CLK), .ZF(alu_5bit_1_cf), .SF(alu_5bit_1_sf), .CF(alu_5bit_1_zf), .dZF(ZF), .dSF(SF), .dCF(CF));
  CU_5bit cu_5bit_1 (
    .Opcode(ram_8x11_1_rd1[10:7]), .ZF(ZF), .SF(SF), .CF(CF), .REG_EN(REG_EN), .OP(OP), .JMP_SEL(JMP_SEL),
    .Imm_Sel(IMM_SEL), .LD_SEL(LD_SEL));
  Reg_4X5 reg_4x5_1 (
    .InE(InE), .REG_EN(REG_EN), .Wr(JMP_ADR[2:1]), .CLK(CPU_CLK), .Wrd(multiplexer_3_out), .InD(InD),
    .Ra(JMP_ADR[2:1]), .Rb({JMP_ADR[0], ram_8x11_1_rd1[3]}), .A(reg_4x5_1_a), .R0(REG0), .R1(REG1),
    .R2(REG2), .R3(REG3), .OutD(OutD), .B(reg_4x5_1_b));
  Multiplexer #(.width(5)) multiplexer_2 (
    .in0(reg_4x5_1_b), .in1({JMP_ADR[0], ram_8x11_1_rd1[3:0]}), .out({multiplexer_2_out, Ld_Adr}),
    .sel(IMM_SEL));
  ALU_5bit alu_5bit_1 (
    .A(reg_4x5_1_a), .B({multiplexer_2_out, Ld_Adr}), .Op(OP), .R(alu_5bit_1_r), .SF(alu_5bit_1_sf),
    .ZF(alu_5bit_1_zf), .CF(alu_5bit_1_cf));
  Multiplexer #(.width(5)) multiplexer_3 (.in0(alu_5bit_1_r), .in1(LD_data), .out(multiplexer_3_out), .sel(LD_SEL));

  // Other names for the same wires on the sheet: D0[10:0] = RAM0; D1[10:0] = RAM1; D2[10:0] = RAM2; D3[10:0] = RAM3;
  //   D4[10:0] = RAM4; D5[10:0] = RAM5; D6[10:0] = RAM6; D7[10:0] = RAM7; R0[4:0] = REG0; R1[4:0] = REG1;
  //   R2[4:0] = REG2; R3[4:0] = REG3
endmodule

module ALU_1bit_Adder (
  input  a,
  input  b,
  input  Cin,
  output S,
  output Cout
);

  wire and_1_out, and_2_out, xor_1_out;

  xor xor_1 (xor_1_out, a, b);
  and and_1 (and_1_out, b, a);
  xor xor_2 (S, xor_1_out, Cin);
  and and_2 (and_2_out, Cin, xor_1_out);
  or or_1 (Cout, and_2_out, and_1_out);
endmodule
