// Logisim project RF.circ as structural Verilog: 4 circuits, main circuit Reg1bit
module Reg1bit (
  input  Din,
  input  Sel,
  input  CLK,
  output Dout
);

  wire multiplexer_1_out;

  D_Flip_Flop d_ff_1 (.D(multiplexer_1_out), .clk(CLK), .Q(Dout));  // open: Qn, preset, reset
  Multiplexer multiplexer_1 (.in0(Dout), .in1(Din), .out(multiplexer_1_out), .sel(Sel));
endmodule

module Reg2bit (
  input  [1:0] Din,
  input  Sel,
  input  CLK,
  output [1:0] Dout
);

  Reg1bit reg1bit_1 (.Din(Din[0]), .Sel(Sel), .CLK(CLK), .Dout(Dout[0]));
  Reg1bit reg1bit_2 (.Din(Din[1]), .Sel(Sel), .CLK(CLK), .Dout(Dout[1]));
endmodule

module Reg3bit (
  input  [2:0] Din,
  input  Sel,
  input  CLK,
  output [2:0] Dout
);

  Reg1bit reg1bit_1 (.Din(Din[0]), .Sel(Sel), .CLK(CLK), .Dout(Dout[0]));
  Reg1bit reg1bit_2 (.Din(Din[1]), .Sel(Sel), .CLK(CLK), .Dout(Dout[1]));
  Reg1bit reg1bit_3 (.Din(Din[2]), .Sel(Sel), .CLK(CLK), .Dout(Dout[2]));
endmodule

module Reg4bit (
  input  [3:0] Din,
  input  Sel,
  input  CLK,
  output [3:0] Dout
);

  Reg1bit reg1bit_1 (.Din(Din[0]), .Sel(Sel), .CLK(CLK), .Dout(Dout[0]));
  Reg1bit reg1bit_2 (.Din(Din[1]), .Sel(Sel), .CLK(CLK), .Dout(Dout[1]));
  Reg1bit reg1bit_3 (.Din(Din[2]), .Sel(Sel), .CLK(CLK), .Dout(Dout[2]));
  Reg1bit reg1bit_4 (.Din(Din[3]), .Sel(Sel), .CLK(CLK), .Dout(Dout[3]));
endmodule
