// Logisim project RegisterSet_8X4.circ as structural Verilog: 4 circuits, main circuit RF1bit
module RF1bit (
  input  Din,
  input  Sel,
  input  CLK,
  output Dout
);

  wire multiplexer_1_out;

  Multiplexer multiplexer_1 (.in0(Dout), .in1(Din), .out(multiplexer_1_out), .sel(Sel));
  D_Flip_Flop d_ff_1 (.D(multiplexer_1_out), .clk(CLK), .Q(Dout));  // open: Qn, preset, reset
endmodule

module RF4bit (
  input  [3:0] Din,
  input  Sel,
  input  CLK,
  output [3:0] Dout
);

  RF1bit rf1bit_1 (.Din(Din[0]), .Sel(Sel), .CLK(CLK), .Dout(Dout[0]));
  RF1bit rf1bit_2 (.Din(Din[1]), .Sel(Sel), .CLK(CLK), .Dout(Dout[1]));
  RF1bit rf1bit_3 (.Din(Din[2]), .Sel(Sel), .CLK(CLK), .Dout(Dout[2]));
  RF1bit rf1bit_4 (.Din(Din[3]), .Sel(Sel), .CLK(CLK), .Dout(Dout[3]));
endmodule

module RegSet (
  input  REG_EN,
  input  [2:0] Wr,
  input  [2:0] Ra,
  input  [3:0] Wrd,
  input  [2:0] Rb,
  input  CLK,
  output [3:0] A,
  output [3:0] B
);

  wire Reg0, Reg1, Reg2, Reg3, Reg4, Reg5, Reg6, Reg7;
  wire [3:0] R0, R1, R2, R3, R4, R5, R6, R7;

  Decoder #(.select(3)) decoder_1 (
    .out0(Reg0), .out1(Reg1), .out2(Reg2), .out3(Reg3), .out4(Reg4), .out5(Reg5), .out6(Reg6), .out7(Reg7),
    .sel(Wr), .en(REG_EN));
  RF4bit rf4bit_1 (.Din(Wrd), .Sel(Reg0), .CLK(CLK), .Dout(R0));
  RF4bit rf4bit_2 (.Din(Wrd), .Sel(Reg1), .CLK(CLK), .Dout(R1));
  RF4bit rf4bit_3 (.Din(Wrd), .Sel(Reg2), .CLK(CLK), .Dout(R2));
  RF4bit rf4bit_4 (.Din(Wrd), .Sel(Reg3), .CLK(CLK), .Dout(R3));
  RF4bit rf4bit_5 (.Din(Wrd), .Sel(Reg4), .CLK(CLK), .Dout(R4));
  RF4bit rf4bit_6 (.Din(Wrd), .Sel(Reg5), .CLK(CLK), .Dout(R5));
  RF4bit rf4bit_7 (.Din(Wrd), .Sel(Reg6), .CLK(CLK), .Dout(R6));
  RF4bit rf4bit_8 (.Din(Wrd), .Sel(Reg7), .CLK(CLK), .Dout(R7));
  Multiplexer #(.select(3), .width(4)) multiplexer_1 (
    .in0(R0), .in1(R1), .in2(R2), .in3(R3), .in4(R4), .in5(R5), .in6(R6), .in7(R7), .out(A), .sel(Ra));
  Multiplexer #(.select(3), .width(4)) multiplexer_2 (
    .in0(R0), .in1(R1), .in2(R2), .in3(R3), .in4(R4), .in5(R5), .in6(R6), .in7(R7), .out(B), .sel(Rb));
endmodule

module FlagReg (
  input  CF,
  input  SF,
  input  ZF,
  input  CLK,
  output CF_out,
  output SF_out,
  output ZF_out
);

  RF1bit rf1bit_1 (.Din(CF), .Sel(1'b1), .CLK(CLK), .Dout(CF_out));
  RF1bit rf1bit_2 (.Din(SF), .Sel(1'b1), .CLK(CLK), .Dout(SF_out));
  RF1bit rf1bit_3 (.Din(ZF), .Sel(1'b1), .CLK(CLK), .Dout(ZF_out));
endmodule
