// Logisim project SRAM.circ as structural Verilog: 4 circuits, main circuit RAM1X1
module RAM1X1 (
  input  RS1,
  input  WD,
  input  WS,
  input  CLK,
  input  RS2,
  output RD1,
  output RD2
);

  wire d_ff_1_q, multiplexer_1_out;

  Multiplexer multiplexer_1 (.in0(d_ff_1_q), .in1(WD), .out(multiplexer_1_out), .sel(WS));
  D_Flip_Flop d_ff_1 (.D(multiplexer_1_out), .clk(CLK), .Q(d_ff_1_q));  // open: Qn, preset, reset
  and and_1 (RD1, RS1, d_ff_1_q);
  and and_2 (RD2, d_ff_1_q, RS2);
endmodule

module RAM1X2 (
  input  WS,
  input  [1:0] WD,
  input  RS1,
  input  RS2,
  input  CLK,
  output [1:0] RD1,
  output [1:0] RD2
);

  RAM1X1 ram1x1_1 (.WD(WD[0]), .WS(WS), .CLK(CLK), .RS2(RS2), .RS1(RS1), .RD1(RD1[0]), .RD2(RD2[0]));
  RAM1X1 ram1x1_2 (.WD(WD[1]), .WS(WS), .CLK(CLK), .RS2(RS2), .RS1(RS1), .RD1(RD1[1]), .RD2(RD2[1]));
endmodule

module RAM1X3 (
  input  WS,
  input  [2:0] WD,
  input  RS1,
  input  RS2,
  input  CLK,
  output [2:0] RD1,
  output [2:0] RD2
);

  RAM1X1 ram1x1_1 (.WD(WD[2]), .WS(WS), .CLK(CLK), .RS2(RS2), .RS1(RS1), .RD1(RD1[2]), .RD2(RD2[2]));
  RAM1X1 ram1x1_2 (.WD(WD[1]), .WS(WS), .CLK(CLK), .RS2(RS2), .RS1(RS1), .RD1(RD1[1]), .RD2(RD2[1]));
  RAM1X1 ram1x1_3 (.WD(WD[0]), .WS(WS), .CLK(CLK), .RS2(RS2), .RS1(RS1), .RD1(RD1[0]), .RD2(RD2[0]));
endmodule

module RAM1X4 (
  input  WS,
  input  [3:0] WD,
  input  RS1,
  input  RS2,
  input  CLK,
  output [3:0] RD1,
  output [3:0] RD2
);

  RAM1X1 ram1x1_1 (.WD(WD[3]), .WS(WS), .CLK(CLK), .RS2(RS2), .RS1(RS1), .RD1(RD1[3]), .RD2(RD2[3]));
  RAM1X1 ram1x1_2 (.WD(WD[2]), .WS(WS), .CLK(CLK), .RS2(RS2), .RS1(RS1), .RD1(RD1[2]), .RD2(RD2[2]));
  RAM1X1 ram1x1_3 (.WD(WD[1]), .WS(WS), .CLK(CLK), .RS2(RS2), .RS1(RS1), .RD1(RD1[1]), .RD2(RD2[1]));
  RAM1X1 ram1x1_4 (.WD(WD[0]), .WS(WS), .CLK(CLK), .RS2(RS2), .RS1(RS1), .RD1(RD1[0]), .RD2(RD2[0]));
endmodule
