// Logisim project SRAM_4X2.circ as structural Verilog: 3 circuits, main circuit RAM_1X1
module RAM_1X1 (
  input  RS1,
  input  WD,
  input  WS,
  input  CLK,
  input  RS2,
  output RD1,
  output RD2
);

  wire d_ff_1_q, multiplexer_1_out;

  Multiplexer multiplexer_1 (.in0(d_ff_1_q), .in1(WD), .out(multiplexer_1_out), .sel(WS));
  D_Flip_Flop d_ff_1 (.D(multiplexer_1_out), .clk(CLK), .Q(d_ff_1_q));  // open: Qn, preset, reset
  and and_1 (RD1, RS1, d_ff_1_q);
  and and_2 (RD2, d_ff_1_q, RS2);
endmodule

module RAM_1X2 (
  input  WS,
  input  [1:0] WD,
  input  RS1,
  input  RS2,
  input  CLK,
  output [1:0] RD1,
  output [1:0] RD2
);

  RAM_1X1 ram_1x1_1 (.WD(WD[0]), .WS(WS), .CLK(CLK), .RS1(RS1), .RS2(RS2), .RD1(RD1[0]), .RD2(RD2[0]));
  RAM_1X1 ram_1x1_2 (.WD(WD[1]), .WS(WS), .CLK(CLK), .RS1(RS1), .RS2(RS2), .RD1(RD1[1]), .RD2(RD2[1]));
endmodule

module RAAM_4X2 (
  input  [1:0] WD,
  input  WE,
  input  [1:0] WA,
  input  [1:0] RA1,
  input  [1:0] RA2,
  input  CLK,
  output [1:0] RD1,
  output [1:0] RD2
);

  wire RS1_0, RS1_1, RS1_2, RS1_3, RS2_0, RS2_1, RS2_2, RS2_3, W0, W1, W2, W3;
  wire [1:0] RD1_0, RD1_1, RD1_2, RD1_3, RD2_0, RD2_1, RD2_2, RD2_3;

  Decoder #(.select(2)) decoder_1 (.out0(W0), .out1(W1), .out2(W2), .out3(W3), .sel(WA), .en(WE));
  Decoder #(.select(2)) decoder_2 (.out0(RS1_0), .out1(RS1_1), .out2(RS1_2), .out3(RS1_3), .sel(RA1));  // open: en
  Decoder #(.select(2)) decoder_3 (.out0(RS2_0), .out1(RS2_1), .out2(RS2_2), .out3(RS2_3), .sel(RA2));  // open: en
  RAM_1X2 ram_1x2_1 (.WS(W0), .WD(WD), .RS1(RS1_0), .RS2(RS2_0), .CLK(CLK), .RD1(RD1_0), .RD2(RD2_0));
  RAM_1X2 ram_1x2_2 (.WS(W1), .WD(WD), .RS1(RS1_1), .RS2(RS2_1), .CLK(CLK), .RD1(RD1_1), .RD2(RD2_1));
  RAM_1X2 ram_1x2_3 (.WS(W2), .WD(WD), .RS1(RS1_2), .RS2(RS2_2), .CLK(CLK), .RD1(RD1_2), .RD2(RD2_2));
  RAM_1X2 ram_1x2_4 (.WS(W3), .WD(WD), .RS1(RS1_3), .RS2(RS2_3), .CLK(CLK), .RD1(RD1_3), .RD2(RD2_3));
  assign RD1 = RD1_0 | RD1_1 | RD1_2 | RD1_3;  // OR_Gate or_1, 2 bits wide
  assign RD2 = RD2_0 | RD2_1 | RD2_2 | RD2_3;  // OR_Gate or_2, 2 bits wide
endmodule
